// Logisim project CPU.circ as structural Verilog: 18 circuits, main circuit main
module main (
  input  [5:0] RestartManual,
  output [7:0] out_2
);

  wire alucpu_1_zero, and_1_out, bcd_to_7_segment_decoder_5_p1, button_1_out, CLK, control_1_alusrc,
       control_1_branchnotequal, control_1_branchonequal, control_1_memread, control_1_memtoreg,
       control_1_memwrite, control_1_regdst, control_1_regwrite, control_1_reiniciar,
       n7_segment_display_1_p1, n7_segment_display_1_p2, n7_segment_display_2_p2, n7_segment_display_3_p2,
       n7_segment_display_5_p2, n7_segment_display_5_p3, n7_segment_display_7_p2, n7_segment_display_9_p2,
       n7_segment_display_9_p3, n7_segment_display_10_p3, n7_segment_display_10_p4, n7_segment_display_11_p2,
       Reiniciar, sumador_1_cout;
  wire [1:0] control_1_aluop0;
  wire [3:0] alucontrol_1_c;
  wire [4:0] multiplexer_1_out, rom_1_data, rom_1_data_2, rom_1_data_5;
  wire [5:0] rom_1_data_3;
  wire [7:0] alucpu_1_s, archivoderegistros_1_readdata1, archivoderegistros_1_readdata2,
       binary_to_bcd_converter_3_p1, binary_to_bcd_converter_4_p1, binary_to_bcd_converter_5_p1,
       bit_extender_1_out, dataMemory_dout, multiplexer_2_out, multiplexer_3_out, multiplexer_4_out,
       sumador_1_s, sumador_2_s;
  wire [10:0] rom_1_data_4;

  // _7_Segment_Display 7_segment_display_1: pin names not known; wires that end beside it: n7_segment_display_1_p1, n7_segment_display_1_p2
  // BCD_to_7_Segment_decoder bcd_to_7_segment_decoder_1: pin names not known
  // _7_Segment_Display 7_segment_display_2: pin names not known; wires that end beside it: n7_segment_display_1_p2, n7_segment_display_2_p2
  // BCD_to_7_Segment_decoder bcd_to_7_segment_decoder_2: pin names not known
  // _7_Segment_Display 7_segment_display_3: pin names not known; wires that end beside it: n7_segment_display_2_p2, n7_segment_display_3_p2
  // BCD_to_7_Segment_decoder bcd_to_7_segment_decoder_3: pin names not known
  _7_Segment_Display u_7_segment_display_4 ();  // open: g, f, a, b, e, d, c, dp
  // BCD_to_7_Segment_decoder bcd_to_7_segment_decoder_4: pin names not known
  // Binary_to_BCD_converter #(.binvalue(8)) binary_to_bcd_converter_1: pin names not known; wires that end beside it: out_2
  // _7_Segment_Display 7_segment_display_5: pin names not known; wires that end beside it: n7_segment_display_3_p2, n7_segment_display_5_p2, n7_segment_display_5_p3
  // BCD_to_7_Segment_decoder bcd_to_7_segment_decoder_5: pin names not known; wires that end beside it: bcd_to_7_segment_decoder_5_p1, bcd_to_7_segment_decoder_5_p1
  _7_Segment_Display u_7_segment_display_6 ();  // open: g, f, a, b, e, d, c, dp
  // BCD_to_7_Segment_decoder bcd_to_7_segment_decoder_6: pin names not known
  // _7_Segment_Display 7_segment_display_7: pin names not known; wires that end beside it: n7_segment_display_5_p3, n7_segment_display_7_p2
  // BCD_to_7_Segment_decoder bcd_to_7_segment_decoder_7: pin names not known
  _7_Segment_Display u_7_segment_display_8 ();  // open: g, f, a, b, e, d, c, dp
  // BCD_to_7_Segment_decoder bcd_to_7_segment_decoder_8: pin names not known
  // _7_Segment_Display 7_segment_display_9: pin names not known; wires that end beside it: n7_segment_display_7_p2, n7_segment_display_9_p2, n7_segment_display_9_p3
  // BCD_to_7_Segment_decoder bcd_to_7_segment_decoder_9: pin names not known
  // _7_Segment_Display 7_segment_display_10: pin names not known; wires that end beside it: n7_segment_display_9_p2, n7_segment_display_9_p3, n7_segment_display_10_p3, n7_segment_display_10_p4
  // BCD_to_7_Segment_decoder bcd_to_7_segment_decoder_10: pin names not known
  Register PC (.D(multiplexer_3_out), .en(CLK), .clk(CLK), .Q(out_2), .clr(Reiniciar));
  // _7_Segment_Display 7_segment_display_11: pin names not known; wires that end beside it: n7_segment_display_10_p4, n7_segment_display_11_p2
  _7_Segment_Display u_7_segment_display_12 ();  // open: g, f, a, b, e, d, c, dp
  // BCD_to_7_Segment_decoder bcd_to_7_segment_decoder_11: pin names not known
  // BCD_to_7_Segment_decoder bcd_to_7_segment_decoder_12: pin names not known
  Sumador sumador_1 (.A(8'h1), .B(out_2), .Cout(sumador_1_cout), .S(sumador_1_s));
  _7_Segment_Display u_7_segment_display_13 ();  // open: g, f, a, b, e, d, c, dp
  // BCD_to_7_Segment_decoder bcd_to_7_segment_decoder_13: pin names not known
  ROM #(.dataWidth(32)) rom_1 (
    .addr(out_2), .data({rom_1_data_3, rom_1_data_2, rom_1_data, rom_1_data_5, rom_1_data_4}));
  _7_Segment_Display u_7_segment_display_14 ();  // open: g, f, a, b, e, d, c, dp
  // BCD_to_7_Segment_decoder bcd_to_7_segment_decoder_14: pin names not known
  // Binary_to_BCD_converter #(.binvalue(8)) binary_to_bcd_converter_2: pin names not known; wires that end beside it: out_2
  LED AUTODESTRUCCION (.in(Reiniciar));
  _7_Segment_Display u_7_segment_display_15 ();  // open: g, f, a, b, e, d, c, dp
  // BCD_to_7_Segment_decoder bcd_to_7_segment_decoder_15: pin names not known
  // Binary_to_BCD_converter #(.binvalue(8)) binary_to_bcd_converter_3: pin names not known; wires that end beside it: binary_to_bcd_converter_3_p1, n7_segment_display_1_p1, n7_segment_display_1_p2, n7_segment_display_2_p2
  // Binary_to_BCD_converter #(.binvalue(8)) binary_to_bcd_converter_4: pin names not known; wires that end beside it: binary_to_bcd_converter_4_p1, n7_segment_display_5_p2, n7_segment_display_5_p3, n7_segment_display_7_p2
  // Binary_to_BCD_converter #(.binvalue(8)) binary_to_bcd_converter_5: pin names not known; wires that end beside it: binary_to_bcd_converter_5_p1, n7_segment_display_10_p3, n7_segment_display_10_p4, n7_segment_display_11_p2
  Clock clock_1 (.out(CLK));
  Control control_1 (
    .OPCODE(rom_1_data_3), .Reiniciar(control_1_reiniciar), .BranchNotEqual(control_1_branchnotequal),
    .ALUOP1(control_1_aluop0[1]), .ALUOP0(control_1_aluop0[0]), .RegDst(control_1_regdst),
    .ALUSrc(control_1_alusrc), .MemToReg(control_1_memtoreg), .RegWrite(control_1_regwrite),
    .MemRead(control_1_memread), .MemWrite(control_1_memwrite), .BranchOnEqual(control_1_branchonequal));
  Button button_1 (.out(button_1_out));
  or or_1 (Reiniciar, control_1_reiniciar, button_1_out);
  Multiplexer #(.width(5)) multiplexer_1 (
    .in0(rom_1_data), .in1(rom_1_data_5), .out(multiplexer_1_out), .sel(control_1_regdst));
  ArchivoDeRegistros archivoderegistros_1 (
    .readRegister1(rom_1_data_2), .readRegister2(rom_1_data), .writeRegister(multiplexer_1_out),
    .writeData(multiplexer_4_out), .regWrite(control_1_regwrite), .Reiniciar(Reiniciar), .CLK(CLK),
    .A(binary_to_bcd_converter_3_p1), .B(binary_to_bcd_converter_4_p1), .C(binary_to_bcd_converter_5_p1),
    .readData1(archivoderegistros_1_readdata1), .readData2(archivoderegistros_1_readdata2));
  Bit_Extender #(.in_width(16), .out_width(8), .\type ("zero")) bit_extender_1 (
    .in({rom_1_data_5, rom_1_data_4}), .out(bit_extender_1_out));
  ALUControl alucontrol_1 (.FUNCT(rom_1_data_4[5:0]), .ALUOP(control_1_aluop0), .C(alucontrol_1_c));
  Multiplexer #(.width(8)) multiplexer_2 (
    .in0(archivoderegistros_1_readdata2), .in1(bit_extender_1_out), .out(multiplexer_2_out),
    .sel(control_1_alusrc));
  ALUCPU alucpu_1 (
    .A(archivoderegistros_1_readdata1), .B(multiplexer_2_out), .C(alucontrol_1_c), .Zero(alucpu_1_zero),
    .S(alucpu_1_s));  // open: Cout
  Sumador sumador_2 (.A(sumador_1_s), .B(bit_extender_1_out), .S(sumador_2_s));  // open: Cout
  Multiplexer #(.width(8)) multiplexer_3 (
    .in0(sumador_1_s), .in1(sumador_2_s), .out(multiplexer_3_out), .sel(and_1_out));
  and and_1 (and_1_out, control_1_branchonequal, alucpu_1_zero);
  RAM dataMemory (
    .addr(alucpu_1_s), .we(control_1_memwrite), .oe(control_1_memread), .clk(CLK),
    .din(archivoderegistros_1_readdata2), .dout(dataMemory_dout));
  Multiplexer #(.width(8)) multiplexer_4 (
    .in0(alucpu_1_s), .in1(dataMemory_dout), .out(multiplexer_4_out), .sel(control_1_memtoreg));
  // also tied to GND on the sheet: sumador_1_cout

  // Notes on the sheet:
  //   +1
  //   ADD-PC
  //   contents of rom_1 (hex, n*v repeats v):
  //   20210000 20420001 20630000 208400e9 221820 400820 601020 0 1432fff9 0 fc000000 0 fc000000
endmodule

module ALU (
  input  [7:0] A,
  input  [3:0] C,
  input  [7:0] B,
  output Zero,
  output Cout,
  output [7:0] S
);

  wire [1:0] sumador_1_cout;
  wire [4:0] compand_1_s, compnand_1_s, compnor_1_s, compor_1_s, compxnor_1_s, compxor_1_s, restador_1_s,
       sumador_1_s;
  wire [7:0] sumador_1_s_2, sumador_1_s_3, sumador_1_s_4;

  Sumador sumador_1 (
    .A(A), .B(B), .Cout(sumador_1_cout[0]),
    .S({sumador_1_s_4[0], sumador_1_s_3[0], sumador_1_s_2[0], sumador_1_s}));
  Restador restador_1 (
    .A(A), .B(B), .Cout(sumador_1_cout[1]),
    .S({sumador_1_s_4[1], sumador_1_s_3[1], sumador_1_s_2[1], restador_1_s}));
  CompOR compor_1 (.A(A), .B(B), .S({sumador_1_s_4[2], sumador_1_s_3[2], sumador_1_s_2[2], compor_1_s}));
  CompAND compand_1 (.A(A), .B(B), .S({sumador_1_s_4[3], sumador_1_s_3[3], sumador_1_s_2[3], compand_1_s}));
  CompXOR compxor_1 (.A(A), .B(B), .S({sumador_1_s_4[4], sumador_1_s_3[4], sumador_1_s_2[4], compxor_1_s}));
  CompNAND compnand_1 (.A(A), .B(B), .S({sumador_1_s_4[5], sumador_1_s_3[5], sumador_1_s_2[5], compnand_1_s}));
  CompNOR compnor_1 (.A(A), .B(B), .S({sumador_1_s_4[6], sumador_1_s_3[6], sumador_1_s_2[6], compnor_1_s}));
  CompXNOR compxnor_1 (.A(A), .B(B), .S({sumador_1_s_4[7], sumador_1_s_3[7], sumador_1_s_2[7], compxnor_1_s}));
  SelectorMUX16 selectormux16_1 (.in_1(C), .in_2({{14{1'b0}}, sumador_1_cout}), .S(Cout));
  SelectorMUX16 selectormux16_2 (
    .in_1(C),
    .in_2({{8{1'b0}}, compxnor_1_s[0], compnor_1_s[0], compnand_1_s[0], compxor_1_s[0], compand_1_s[0], compor_1_s[0], restador_1_s[0], sumador_1_s[0]}),
    .S(S[0]));
  SelectorMUX16 selectormux16_3 (
    .in_1(C),
    .in_2({{8{1'b0}}, compxnor_1_s[1], compnor_1_s[1], compnand_1_s[1], compxor_1_s[1], compand_1_s[1], compor_1_s[1], restador_1_s[1], sumador_1_s[1]}),
    .S(S[1]));
  SelectorMUX16 selectormux16_4 (
    .in_1(C),
    .in_2({{8{1'b0}}, compxnor_1_s[2], compnor_1_s[2], compnand_1_s[2], compxor_1_s[2], compand_1_s[2], compor_1_s[2], restador_1_s[2], sumador_1_s[2]}),
    .S(S[2]));
  SelectorMUX16 selectormux16_5 (
    .in_1(C),
    .in_2({{8{1'b0}}, compxnor_1_s[3], compnor_1_s[3], compnand_1_s[3], compxor_1_s[3], compand_1_s[3], compor_1_s[3], restador_1_s[3], sumador_1_s[3]}),
    .S(S[3]));
  ExactlyOne xor_1 (
    .out(Zero), .in0(S[0]), .in1(S[1]), .in2(S[2]), .in3(S[3]), .in4(1'b1), .in5(S[4]), .in6(S[5]),
    .in7(S[6]), .in8(S[7]));
  SelectorMUX16 selectormux16_6 (
    .in_1(C),
    .in_2({{8{1'b0}}, compxnor_1_s[4], compnor_1_s[4], compnand_1_s[4], compxor_1_s[4], compand_1_s[4], compor_1_s[4], restador_1_s[4], sumador_1_s[4]}),
    .S(S[4]));
  SelectorMUX16 selectormux16_7 (.in_1(C), .in_2({{8{1'b0}}, sumador_1_s_2}), .S(S[5]));
  SelectorMUX16 selectormux16_8 (.in_1(C), .in_2({{8{1'b0}}, sumador_1_s_3}), .S(S[6]));
  SelectorMUX16 selectormux16_9 (.in_1(C), .in_2({{8{1'b0}}, sumador_1_s_4}), .S(S[7]));

  // Notes on the sheet:
  //   ZONA DE PRUEBA
  //   N
  //   Operación
  //   0   Sumar
  //   1   Restar
  //   2   OR
  //   3   AND
  //   4   XOR
  //   5   NAND
  //   6   NOR
  //   7   XNOR
  //   Bin
  //   000
  //   001
  //   010
  //   011
  //   100
  //   101
  //   110
  //   111
endmodule

module ALUCPU (
  input  [7:0] A,
  input  [3:0] C,
  input  [7:0] B,
  output Cout,
  output [7:0] S,
  output Zero
);

  wire [6:0] compand_1_s, compand_1_s_2, compand_1_s_3, compand_1_s_4, compand_1_s_5, compand_1_s_6,
       compand_1_s_7, compand_1_s_8;
  wire [6:2] sumador_1_cout;

  CompAND compand_1 (
    .A(A), .B(B),
    .S({compand_1_s_8[0], compand_1_s_7[0], compand_1_s_6[0], compand_1_s_5[0], compand_1_s_4[0], compand_1_s_3[0], compand_1_s_2[0], compand_1_s[0]}));
  CompOR compor_1 (
    .A(A), .B(B),
    .S({compand_1_s_8[1], compand_1_s_7[1], compand_1_s_6[1], compand_1_s_5[1], compand_1_s_4[1], compand_1_s_3[1], compand_1_s_2[1], compand_1_s[1]}));
  Sumador sumador_1 (
    .A(A), .B(B), .Cout(sumador_1_cout[2]),
    .S({compand_1_s_8[2], compand_1_s_7[2], compand_1_s_6[2], compand_1_s_5[2], compand_1_s_4[2], compand_1_s_3[2], compand_1_s_2[2], compand_1_s[2]}));
  Restador restador_1 (
    .A(A), .B(B), .Cout(sumador_1_cout[6]),
    .S({compand_1_s_8[6], compand_1_s_7[6], compand_1_s_6[6], compand_1_s_5[6], compand_1_s_4[6], compand_1_s_3[6], compand_1_s_2[6], compand_1_s[6]}));
  SelectorMUX16 selectormux16_1 (
    .in_1(C), .in_2({{9{1'b0}}, sumador_1_cout[6], 3'b000, sumador_1_cout[2], 2'b00}), .S(Cout));
  ExactlyOne xor_1 (
    .out(Zero), .in0(S[0]), .in1(S[1]), .in2(S[2]), .in3(S[3]), .in4(1'b1), .in5(S[4]), .in6(S[5]),
    .in7(S[6]), .in8(S[7]));
  SelectorMUX16 selectormux16_2 (.in_1(C), .in_2({{9{1'b0}}, compand_1_s[6], 3'b000, compand_1_s[2:0]}), .S(S[0]));
  SelectorMUX16 selectormux16_3 (.in_1(C), .in_2({{9{1'b0}}, compand_1_s_2[6], 3'b000, compand_1_s_2[2:0]}), .S(S[1]));
  SelectorMUX16 selectormux16_4 (.in_1(C), .in_2({{9{1'b0}}, compand_1_s_3[6], 3'b000, compand_1_s_3[2:0]}), .S(S[2]));
  SelectorMUX16 selectormux16_5 (.in_1(C), .in_2({{9{1'b0}}, compand_1_s_4[6], 3'b000, compand_1_s_4[2:0]}), .S(S[3]));
  SelectorMUX16 selectormux16_6 (.in_1(C), .in_2({{9{1'b0}}, compand_1_s_5[6], 3'b000, compand_1_s_5[2:0]}), .S(S[4]));
  SelectorMUX16 selectormux16_7 (.in_1(C), .in_2({{9{1'b0}}, compand_1_s_6[6], 3'b000, compand_1_s_6[2:0]}), .S(S[5]));
  SelectorMUX16 selectormux16_8 (.in_1(C), .in_2({{9{1'b0}}, compand_1_s_7[6], 3'b000, compand_1_s_7[2:0]}), .S(S[6]));
  SelectorMUX16 selectormux16_9 (.in_1(C), .in_2({{9{1'b0}}, compand_1_s_8[6], 3'b000, compand_1_s_8[2:0]}), .S(S[7]));

  // Notes on the sheet:
  //   ZONA DE PRUEBA
  //   N
  //   0
  //   1
  //   2
  //   6
  //   0000
  //   0001
  //   0010
  //   0110
  //   Operación
  //   AND
  //   OR
  //   SUMA
  //   RESTA
  //   Bin
  //   0000
  //   0001
  //   0010
  //   0110
endmodule

module SelectorMUX16 (
  input  [3:0] in_1,
  input  [15:0] in_2,
  output S
);

  wire and_1_out, and_2_out, and_3_out, and_4_out, and_5_out, and_6_out, and_7_out, and_8_out, and_9_out,
       and_10_out, and_11_out, and_12_out, and_13_out, and_14_out, and_15_out, and_16_out, not_1_out,
       not_2_out, not_3_out, not_4_out;

  not not_1 (not_1_out, in_1[3]);
  not not_2 (not_2_out, in_1[2]);
  not not_3 (not_3_out, in_1[1]);
  not not_4 (not_4_out, in_1[0]);
  and and_1 (and_1_out, in_2[0], not_4_out, not_3_out, not_2_out, not_1_out);
  and and_2 (and_2_out, in_2[1], in_1[0], not_3_out, not_2_out, not_1_out);
  and and_3 (and_3_out, in_2[2], not_4_out, in_1[1], not_2_out, not_1_out);
  and and_4 (and_4_out, in_2[3], in_1[0], in_1[1], not_2_out, not_1_out);
  and and_5 (and_5_out, in_2[4], not_4_out, not_3_out, in_1[2], not_1_out);
  and and_6 (and_6_out, in_2[5], in_1[0], not_3_out, in_1[2], not_1_out);
  and and_7 (and_7_out, in_2[6], not_4_out, in_1[1], in_1[2], not_1_out);
  and and_8 (and_8_out, in_2[7], in_1[0], in_1[1], in_1[2], not_1_out);
  and and_9 (and_9_out, in_2[8], not_4_out, not_3_out, not_2_out, in_1[3]);
  and and_10 (and_10_out, in_2[9], in_1[0], not_3_out, not_2_out, in_1[3]);
  and and_11 (and_11_out, in_2[10], not_4_out, in_1[1], not_2_out, in_1[3]);
  and and_12 (and_12_out, in_2[11], in_1[0], in_1[1], not_2_out, in_1[3]);
  and and_13 (and_13_out, in_2[12], not_4_out, not_3_out, in_1[2], in_1[3]);
  and and_14 (and_14_out, in_2[13], in_1[0], not_3_out, in_1[2], in_1[3]);
  and and_15 (and_15_out, in_2[14], not_4_out, in_1[1], in_1[2], in_1[3]);
  and and_16 (and_16_out, in_2[15], in_1[0], in_1[1], in_1[2], in_1[3]);
  or or_1 (S, and_1_out, and_2_out, and_3_out, and_4_out, and_5_out, and_6_out, and_7_out, and_8_out, and_9_out, and_10_out, and_11_out, and_12_out, and_13_out, and_14_out, and_15_out, and_16_out);
endmodule

module FullAdderCasero (
  input  A,
  input  B,
  input  Cin,
  output S,
  output Cout
);

  wire and_1_out, and_2_out, xor_1_out;

  xor xor_1 (xor_1_out, A, B);
  Adder adder_1 ();  // open: a, b, out, cin, cout
  xor xor_2 (S, xor_1_out, Cin);
  and and_1 (and_1_out, Cin, xor_1_out);
  and and_2 (and_2_out, B, A);
  or or_1 (Cout, and_1_out, and_2_out);

  // Notes on the sheet:
  //   Full Adder Casero
endmodule

module Sumador (
  input  [7:0] A,
  input  [7:0] B,
  output Cout,
  output [7:0] S
);

  wire fulladdercasero_2_cout, fulladdercasero_3_cout, fulladdercasero_4_cout, fulladdercasero_5_cout,
       fulladdercasero_6_cout, fulladdercasero_7_cout, fulladdercasero_8_cout;

  FullAdderCasero fulladdercasero_1 (.A(A[7]), .B(B[7]), .Cin(fulladdercasero_2_cout), .S(S[7]), .Cout(Cout));
  FullAdderCasero fulladdercasero_2 (
    .A(A[6]), .B(B[6]), .Cin(fulladdercasero_3_cout), .S(S[6]), .Cout(fulladdercasero_2_cout));
  FullAdderCasero fulladdercasero_3 (
    .A(A[5]), .B(B[5]), .Cin(fulladdercasero_4_cout), .S(S[5]), .Cout(fulladdercasero_3_cout));
  FullAdderCasero fulladdercasero_4 (
    .A(A[4]), .B(B[4]), .Cin(fulladdercasero_5_cout), .S(S[4]), .Cout(fulladdercasero_4_cout));
  FullAdderCasero fulladdercasero_5 (
    .A(A[3]), .B(B[3]), .Cin(fulladdercasero_6_cout), .S(S[3]), .Cout(fulladdercasero_5_cout));
  FullAdderCasero fulladdercasero_6 (
    .A(A[2]), .B(B[2]), .Cin(fulladdercasero_7_cout), .S(S[2]), .Cout(fulladdercasero_6_cout));
  Adder adder_1 ();  // open: a, b, out, cin, cout
  FullAdderCasero fulladdercasero_7 (
    .A(A[1]), .B(B[1]), .Cin(fulladdercasero_8_cout), .S(S[1]), .Cout(fulladdercasero_7_cout));
  FullAdderCasero fulladdercasero_8 (.A(A[0]), .B(B[0]), .Cin(1'b0), .S(S[0]), .Cout(fulladdercasero_8_cout));

  // Notes on the sheet:
  //   +
  //   --------------------
  //   Sumador Casero
endmodule

module Restador (
  input  [7:0] A,
  input  [7:0] B,
  output Cout,
  output [7:0] S
);

  wire B0, B1, B2, B3, B4, B5, B6, B7, fulladdercasero_1_cout, fulladdercasero_2_cout,
       fulladdercasero_3_cout, fulladdercasero_4_cout, fulladdercasero_5_cout, fulladdercasero_6_cout,
       fulladdercasero_7_cout, fulladdercasero_8_cout;

  not not_1 (Cout, fulladdercasero_1_cout);
  FullAdderCasero fulladdercasero_1 (
    .A(A[7]), .B(B7), .Cin(fulladdercasero_2_cout), .S(S[7]), .Cout(fulladdercasero_1_cout));
  FullAdderCasero fulladdercasero_2 (
    .A(A[6]), .B(B6), .Cin(fulladdercasero_3_cout), .S(S[6]), .Cout(fulladdercasero_2_cout));
  FullAdderCasero fulladdercasero_3 (
    .A(A[5]), .B(B5), .Cin(fulladdercasero_4_cout), .S(S[5]), .Cout(fulladdercasero_3_cout));
  assign {B7, B6, B5, B4, B3, B2, B1, B0} = ~B;  // NOT_Gate not_2, 8 bits wide
  FullAdderCasero fulladdercasero_4 (
    .A(A[4]), .B(B4), .Cin(fulladdercasero_5_cout), .S(S[4]), .Cout(fulladdercasero_4_cout));
  FullAdderCasero fulladdercasero_5 (
    .A(A[3]), .B(B3), .Cin(fulladdercasero_6_cout), .S(S[3]), .Cout(fulladdercasero_5_cout));
  FullAdderCasero fulladdercasero_6 (
    .A(A[2]), .B(B2), .Cin(fulladdercasero_7_cout), .S(S[2]), .Cout(fulladdercasero_6_cout));
  Subtractor subtractor_1 ();  // open: a, b, out, bin, bout
  FullAdderCasero fulladdercasero_7 (
    .A(A[1]), .B(B1), .Cin(fulladdercasero_8_cout), .S(S[1]), .Cout(fulladdercasero_7_cout));
  FullAdderCasero fulladdercasero_8 (.A(A[0]), .B(B0), .Cin(1'b1), .S(S[0]), .Cout(fulladdercasero_8_cout));

  // Notes on the sheet:
  //   -
  //   --------------------
  //   Restador Casero
endmodule

module CompOR (
  input  [7:0] A,
  input  [7:0] B,
  output [7:0] S
);

  or or_1 (S[7], A[7], B[7]);
  or or_2 (S[6], A[6], B[6]);
  or or_3 (S[5], A[5], B[5]);
  or or_4 (S[4], A[4], B[4]);
  or or_5 (S[3], A[3], B[3]);
  or or_6 (S[2], A[2], B[2]);
  or or_7 (S[1], A[1], B[1]);
  or or_8 (S[0], A[0], B[0]);

  // Notes on the sheet:
  //   OR
  //   --------------------
endmodule

module CompAND (
  input  [7:0] A,
  input  [7:0] B,
  output [7:0] S
);

  and and_1 (S[7], A[7], B[7]);
  and and_2 (S[6], A[6], B[6]);
  and and_3 (S[5], A[5], B[5]);
  and and_4 (S[4], A[4], B[4]);
  and and_5 (S[3], A[3], B[3]);
  and and_6 (S[2], A[2], B[2]);
  and and_7 (S[1], A[1], B[1]);
  and and_8 (S[0], A[0], B[0]);

  // Notes on the sheet:
  //   AND
  //   --------------------
endmodule

module CompXOR (
  input  [7:0] A,
  input  [7:0] B,
  output [7:0] S
);

  xor xor_1 (S[7], A[7], B[7]);
  xor xor_2 (S[6], A[6], B[6]);
  xor xor_3 (S[5], A[5], B[5]);
  xor xor_4 (S[4], A[4], B[4]);
  xor xor_5 (S[3], A[3], B[3]);
  xor xor_6 (S[2], A[2], B[2]);
  xor xor_7 (S[1], A[1], B[1]);
  xor xor_8 (S[0], A[0], B[0]);

  // Notes on the sheet:
  //   XOR
  //   --------------------
endmodule

module CompNAND (
  input  [7:0] A,
  input  [7:0] B,
  output [7:0] S
);

  nand nand_1 (S[7], A[7], B[7]);
  nand nand_2 (S[6], A[6], B[6]);
  nand nand_3 (S[5], A[5], B[5]);
  nand nand_4 (S[4], A[4], B[4]);
  nand nand_5 (S[3], A[3], B[3]);
  nand nand_6 (S[2], A[2], B[2]);
  nand nand_7 (S[1], A[1], B[1]);
  nand nand_8 (S[0], A[0], B[0]);

  // Notes on the sheet:
  //   NAND
  //   --------------------
endmodule

module CompNOR (
  input  [7:0] A,
  input  [7:0] B,
  output [7:0] S
);

  nor nor_1 (S[7], A[7], B[7]);
  nor nor_2 (S[6], A[6], B[6]);
  nor nor_3 (S[5], A[5], B[5]);
  nor nor_4 (S[4], A[4], B[4]);
  nor nor_5 (S[3], A[3], B[3]);
  nor nor_6 (S[2], A[2], B[2]);
  nor nor_7 (S[1], A[1], B[1]);
  nor nor_8 (S[0], A[0], B[0]);

  // Notes on the sheet:
  //   NOR
  //   --------------------
endmodule

module CompXNOR (
  input  [7:0] A,
  input  [7:0] B,
  output [7:0] S
);

  xnor xnor_1 (S[7], A[7], B[7]);
  xnor xnor_2 (S[6], A[6], B[6]);
  xnor xnor_3 (S[5], A[5], B[5]);
  xnor xnor_4 (S[4], A[4], B[4]);
  xnor xnor_5 (S[3], A[3], B[3]);
  xnor xnor_6 (S[2], A[2], B[2]);
  xnor xnor_7 (S[1], A[1], B[1]);
  xnor xnor_8 (S[0], A[0], B[0]);

  // Notes on the sheet:
  //   XNOR
  //   --------------------
endmodule

module Testeos (
  input  in_1,
  input  [7:0] in_2,
  input  in_3,
  input  in_4,
  input  [31:0] in_5,
  output [7:0] out_6,
  output out_7
);

  wire clock_1_out, not_1_out;
  wire [7:0] controlled_buffer_1_out, undriven;

  assign controlled_buffer_1_out = in_1 ? in_2 : 8'bz;  // Controlled_Buffer controlled_buffer_1
  not not_1 (not_1_out, in_1);
  assign controlled_buffer_1_out = not_1_out ? undriven : 8'bz;  // Controlled_Buffer controlled_buffer_2
  Register register_1 (.D(controlled_buffer_1_out), .en(clock_1_out), .clk(clock_1_out), .Q(out_6), .clr(in_3));
  Clock clock_1 (.out(clock_1_out));
  // Sumador sumador_1: pin names not known; wires that end beside it: 1'b0, 1'b0, 1'b1

  assign out_7 = in_4;

  // Other names for the same wires on the sheet: A = in_4
endmodule

module TESTPANTALLA (
  input  [7:0] in_1,
  input  in_2,
  output [3:0] out_3
);

  wire binary_to_bcd_converter_1_p2, clock_1_out;
  wire [3:0] undriven;

  Register #(.width(4)) register_1 (.D(undriven), .en(clock_1_out), .clk(clock_1_out), .Q(out_3), .clr(in_2));
  Clock clock_1 (.out(clock_1_out));
  // Binary_to_BCD_converter #(.binvalue(4)) binary_to_bcd_converter_1: pin names not known; wires that end beside it: out_3, binary_to_bcd_converter_1_p2
  // Sumador sumador_1: pin names not known; wires that end beside it: 1'b0, 1'b0, 1'b1
  _7_Segment_Display u_7_segment_display_1 ();  // open: g, f, a, b, e, d, c, dp
  // BCD_to_7_Segment_decoder bcd_to_7_segment_decoder_1: pin names not known; wires that end beside it: 1'b0, 1'b0, 1'b0, 1'b0, 1'b0, 1'b0, 1'b0, 1'b0, 1'b0, binary_to_bcd_converter_1_p2
  _7_Segment_Display u_7_segment_display_2 ();  // open: g, f, a, b, e, d, c, dp
  // BCD_to_7_Segment_decoder bcd_to_7_segment_decoder_2: pin names not known
  // Binary_to_BCD_converter #(.binvalue(8)) binary_to_bcd_converter_2: pin names not known; wires that end beside it: in_1
  _7_Segment_Display u_7_segment_display_3 ();  // open: g, f, a, b, e, d, c, dp
  _7_Segment_Display u_7_segment_display_4 ();  // open: g, f, a, b, e, d, c, dp
  // BCD_to_7_Segment_decoder bcd_to_7_segment_decoder_3: pin names not known
  // BCD_to_7_Segment_decoder bcd_to_7_segment_decoder_4: pin names not known
endmodule

module ArchivoDeRegistros (
  input  [4:0] readRegister1,
  input  [4:0] readRegister2,
  input  [4:0] writeRegister,
  input  [7:0] writeData,
  input  regWrite,
  input  Reiniciar,
  input  CLK,
  output [7:0] A,
  output [7:0] readData1,
  output [7:0] B,
  output [7:0] C,
  output [7:0] readData2
);

  wire and_1_out, and_2_out, and_3_out, and_4_out, and_5_out, and_6_out, and_7_out, and_8_out,
       decoder_1_out0, decoder_1_out1, decoder_1_out2, decoder_1_out3, decoder_1_out4, decoder_1_out5,
       decoder_1_out6, decoder_1_out7, decoder_1_out8, decoder_1_out9, decoder_1_out10, decoder_1_out11,
       decoder_1_out12, decoder_1_out13, decoder_1_out14, decoder_1_out15, decoder_1_out16, decoder_1_out17,
       decoder_1_out18, decoder_1_out19, decoder_1_out20, decoder_1_out21, decoder_1_out22, decoder_1_out23,
       decoder_1_out24, decoder_1_out25, decoder_1_out26, decoder_1_out27, decoder_1_out28, decoder_1_out29,
       decoder_1_out30, decoder_1_out31;
  wire [7:0] register_1_q, register_5_q, register_6_q, register_7_q, register_8_q;

  Decoder #(.enable("false"), .select(5)) decoder_1 (
    .out0(decoder_1_out0), .out1(decoder_1_out1), .out2(decoder_1_out2), .out3(decoder_1_out3),
    .out4(decoder_1_out4), .out5(decoder_1_out5), .out6(decoder_1_out6), .out7(decoder_1_out7),
    .out8(decoder_1_out8), .out9(decoder_1_out9), .out10(decoder_1_out10), .out11(decoder_1_out11),
    .out12(decoder_1_out12), .out13(decoder_1_out13), .out14(decoder_1_out14), .out15(decoder_1_out15),
    .out16(decoder_1_out16), .out17(decoder_1_out17), .out18(decoder_1_out18), .out19(decoder_1_out19),
    .out20(decoder_1_out20), .out21(decoder_1_out21), .out22(decoder_1_out22), .out23(decoder_1_out23),
    .out24(decoder_1_out24), .out25(decoder_1_out25), .out26(decoder_1_out26), .out27(decoder_1_out27),
    .out28(decoder_1_out28), .out29(decoder_1_out29), .out30(decoder_1_out30), .out31(decoder_1_out31),
    .sel(writeRegister));
  and and_1 (and_1_out, decoder_1_out0, regWrite);
  and and_2 (and_2_out, decoder_1_out1, regWrite);
  and and_3 (and_3_out, decoder_1_out2, regWrite);
  and and_4 (and_4_out, decoder_1_out3, regWrite);
  and and_5 (and_5_out, decoder_1_out4, regWrite);
  and and_6 (and_6_out, decoder_1_out5, regWrite);
  and and_7 (and_7_out, decoder_1_out6, regWrite);
  and and_8 (and_8_out, decoder_1_out7, regWrite);
  Register register_1 (.D(writeData), .en(and_1_out), .clk(CLK), .Q(register_1_q), .clr(Reiniciar));
  Register register_2 (.D(writeData), .en(and_2_out), .clk(CLK), .Q(A), .clr(Reiniciar));
  Register register_3 (.D(writeData), .en(and_3_out), .clk(CLK), .Q(B), .clr(Reiniciar));
  Register register_4 (.D(writeData), .en(and_4_out), .clk(CLK), .Q(C), .clr(Reiniciar));
  Register register_5 (.D(writeData), .en(and_5_out), .clk(CLK), .Q(register_5_q), .clr(Reiniciar));
  Register register_6 (.D(writeData), .en(and_6_out), .clk(CLK), .Q(register_6_q), .clr(Reiniciar));
  Register register_7 (.D(writeData), .en(and_7_out), .clk(CLK), .Q(register_7_q), .clr(Reiniciar));
  Register register_8 (.D(writeData), .en(and_8_out), .clk(CLK), .Q(register_8_q), .clr(Reiniciar));
  Multiplexer #(.select(5), .width(8)) multiplexer_1 (
    .in0(register_1_q), .in1(A), .in2(B), .in3(C), .in4(register_5_q), .in5(register_6_q),
    .in6(register_7_q), .in7(register_8_q), .out(readData1), .sel(readRegister1));  // open: in8, in9, in10, in11, in12, in13, in14, in15, in16, in17, in18, in19, in20, in21, in22, in23, in24, in25, in26, in27, in28, in29, in30, in31
  Multiplexer #(.select(5), .width(8)) multiplexer_2 (
    .in0(register_1_q), .in1(A), .in2(B), .in3(C), .in4(register_5_q), .in5(register_6_q),
    .in6(register_7_q), .in7(register_8_q), .out(readData2), .sel(readRegister2));  // open: in8, in9, in10, in11, in12, in13, in14, in15, in16, in17, in18, in19, in20, in21, in22, in23, in24, in25, in26, in27, in28, in29, in30, in31
endmodule

module Control (
  input  [5:0] OPCODE,
  output Reiniciar,
  output RegDst,
  output ALUSrc,
  output MemToReg,
  output RegWrite,
  output MemRead,
  output MemWrite,
  output BranchOnEqual,
  output BranchNotEqual,
  output ALUOP1,
  output ALUOP0
);

  wire ADDI_out, not_1_out, not_2_out, not_3_out, not_4_out, not_5_out, not_6_out, not_7_out, not_8_out,
       not_9_out, not_10_out, not_11_out, not_12_out, not_13_out, not_14_out, not_15_out, not_16_out,
       not_17_out, not_18_out, not_19_out, not_20_out, not_21_out, not_22_out, not_23_out, not_24_out,
       not_25_out, SW_out;

  not not_1 (not_1_out, OPCODE[5]);
  not not_2 (not_2_out, OPCODE[4]);
  not not_3 (not_3_out, OPCODE[3]);
  not not_4 (not_4_out, OPCODE[2]);
  and TipoR (RegDst, not_1_out, not_2_out, not_3_out, not_4_out, not_5_out, not_6_out);
  not not_5 (not_5_out, OPCODE[1]);
  not not_6 (not_6_out, OPCODE[0]);
  not not_7 (not_7_out, OPCODE[4]);
  not not_8 (not_8_out, OPCODE[3]);
  not not_9 (not_9_out, OPCODE[2]);
  and LW (MemRead, OPCODE[5], not_7_out, not_8_out, not_9_out, OPCODE[1], OPCODE[0]);
  not not_10 (not_10_out, OPCODE[4]);
  not not_11 (not_11_out, OPCODE[2]);
  and SW (SW_out, OPCODE[5], not_10_out, OPCODE[3], not_11_out, OPCODE[1], OPCODE[0]);
  not not_12 (not_12_out, OPCODE[5]);
  not not_13 (not_13_out, OPCODE[4]);
  not not_14 (not_14_out, OPCODE[3]);
  and BEQ (BranchOnEqual, not_12_out, not_13_out, not_14_out, OPCODE[2], not_15_out, not_16_out);
  not not_15 (not_15_out, OPCODE[1]);
  not not_16 (not_16_out, OPCODE[0]);
  not not_17 (not_17_out, OPCODE[5]);
  not not_18 (not_18_out, OPCODE[4]);
  not not_19 (not_19_out, OPCODE[3]);
  not not_20 (not_20_out, OPCODE[1]);
  and BNE (BranchNotEqual, not_17_out, not_18_out, not_19_out, OPCODE[2], not_20_out, OPCODE[0]);
  not not_21 (not_21_out, OPCODE[5]);
  not not_22 (not_22_out, OPCODE[4]);
  not not_23 (not_23_out, OPCODE[2]);
  not not_24 (not_24_out, OPCODE[1]);
  and ADDI (ADDI_out, not_21_out, not_22_out, OPCODE[3], not_23_out, not_24_out, not_25_out);
  not not_25 (not_25_out, OPCODE[0]);
  and Restart (Reiniciar, OPCODE[0], OPCODE[1], OPCODE[2], OPCODE[3], OPCODE[4], OPCODE[5]);
  or or_1 (ALUSrc, MemRead, ADDI_out, SW_out);
  or or_2 (RegWrite, RegDst, ADDI_out, MemRead);
  or or_3 (MemWrite, ADDI_out, SW_out);
  or or_4 (ALUOP1, RegDst, ADDI_out);
  or or_5 (ALUOP0, BranchNotEqual, BranchOnEqual);

  assign MemToReg = MemRead;
endmodule

module ALUControl (
  input  [5:0] FUNCT,
  input  [1:0] ALUOP,
  output [3:0] C
);

  wire and_1_out, not_1_out, not_2_out;

  and and_1 (and_1_out, FUNCT[1], ALUOP[1]);
  and and_2 (C[0], FUNCT[2], FUNCT[0], ALUOP[1]);
  or or_1 (C[2], ALUOP[0], and_1_out);
  not not_1 (not_1_out, FUNCT[2]);
  or or_2 (C[1], not_1_out, not_2_out);
  not not_2 (not_2_out, ALUOP[1]);

  assign C[3] = 1'b0;
endmodule
